// Logisim project jrmips.circ as structural Verilog: 11 circuits, main circuit Register File
module Register_File (
  input  [1:0] WriteSource,
  input  [2:0] read_reg1,
  input  [15:0] Write_Data,
  input  [15:0] HI,
  input  [15:0] LO,
  input  [2:0] WriteRegister,
  input  enable_write,
  input  [2:0] Write_Register_Enabler,
  input  [2:0] read_reg2,
  input  Clock,
  output [15:0] read_data1,
  output [15:0] read_data2
);

  wire decoder_1_out0, decoder_1_out1, decoder_1_out2, decoder_1_out3, decoder_1_out4, decoder_1_out5,
       decoder_1_out6, decoder_1_out7;
  wire [15:0] demultiplexer_1_out0, demultiplexer_1_out1, demultiplexer_1_out2, demultiplexer_1_out3,
       demultiplexer_1_out4, demultiplexer_1_out5, demultiplexer_1_out6, demultiplexer_1_out7,
       multiplexer_1_out, r0_q, r1_q, r2_q, r3_q, r4_q, r5_q, r6_q, r7_q;

  Multiplexer #(.select(2), .width(16)) multiplexer_1 (
    .in0(Write_Data), .in1(HI), .in2(LO), .out(multiplexer_1_out), .sel(WriteSource), .en(enable_write));  // open: in3
  Demultiplexer #(.select(3), .width(16)) demultiplexer_1 (
    .out0(demultiplexer_1_out0), .out1(demultiplexer_1_out1), .out2(demultiplexer_1_out2),
    .out3(demultiplexer_1_out3), .out4(demultiplexer_1_out4), .out5(demultiplexer_1_out5),
    .out6(demultiplexer_1_out6), .out7(demultiplexer_1_out7), .in(multiplexer_1_out), .sel(WriteRegister));  // open: en
  Decoder_part #(.select(3)) decoder_1 (
    .out0(decoder_1_out0), .out1(decoder_1_out1), .out2(decoder_1_out2), .out3(decoder_1_out3),
    .out4(decoder_1_out4), .out5(decoder_1_out5), .out6(decoder_1_out6), .out7(decoder_1_out7),
    .sel(Write_Register_Enabler));  // open: en
  Register #(.width(16)) r0 (.D(demultiplexer_1_out0), .en(decoder_1_out0), .Q(r0_q), .clk(Clock));  // open: clr
  Register #(.width(16)) r1 (.D(demultiplexer_1_out1), .en(decoder_1_out1), .Q(r1_q), .clk(Clock));  // open: clr
  Register #(.width(16)) r2 (.D(demultiplexer_1_out2), .en(decoder_1_out2), .Q(r2_q), .clk(Clock));  // open: clr
  Register #(.width(16)) r3 (.D(demultiplexer_1_out3), .en(decoder_1_out3), .Q(r3_q), .clk(Clock));  // open: clr
  Register #(.width(16)) r4 (.D(demultiplexer_1_out4), .en(decoder_1_out4), .Q(r4_q), .clk(Clock));  // open: clr
  Register #(.width(16)) r5 (.D(demultiplexer_1_out5), .en(decoder_1_out5), .Q(r5_q), .clk(Clock));  // open: clr
  Register #(.width(16)) r6 (.D(demultiplexer_1_out6), .en(decoder_1_out6), .Q(r6_q), .clk(Clock));  // open: clr
  Register #(.width(16)) r7 (.D(demultiplexer_1_out7), .en(decoder_1_out7), .Q(r7_q), .clk(Clock));  // open: clr
  Multiplexer #(.select(3), .width(16)) multiplexer_2 (
    .in0(r0_q), .in1(r1_q), .in2(r2_q), .in3(r3_q), .in4(r4_q), .in5(r5_q), .in6(r6_q), .in7(r7_q),
    .out(read_data1), .sel(read_reg1));  // open: en
  Multiplexer #(.select(3), .width(16)) multiplexer_3 (
    .in0(r0_q), .in1(r1_q), .in2(r2_q), .in3(r3_q), .in4(r4_q), .in5(r5_q), .in6(r6_q), .in7(r7_q),
    .out(read_data2), .sel(read_reg2));  // open: en
endmodule

module ALU (
  input  [15:0] ALU_op1,
  input  [15:0] ALU_op2,
  input  [1:0] Opcode,
  input  [1:0] BranchOp,
  input  Subop,
  output branch_y_n,
  output [15:0] ALU_output
);

  wire comparator_1_eq, comparator_1_gt, comparator_1_lt, not_3_out;
  wire [15:0] adder_1_out, adder_2_out, and_1_out, multiplexer_1_out, multiplexer_2_out, multiplexer_4_out,
       not_1_out, not_2_out, subtractor_1_out;

  assign not_1_out = ~ALU_op1;  // NOT_Gate not_1, 16 bits wide
  assign not_2_out = ~ALU_op2;  // NOT_Gate not_2, 16 bits wide
  Comparator #(.width(16)) comparator_1 (
    .a(ALU_op1), .b({16{1'b0}}), .gt(comparator_1_gt), .eq(comparator_1_eq), .lt(comparator_1_lt));
  not not_3 (not_3_out, comparator_1_eq);
  Multiplexer #(.width(16)) multiplexer_1 (
    .in0(ALU_op1), .in1(not_1_out), .out(multiplexer_1_out), .sel(Subop));  // open: en
  Multiplexer #(.width(16)) multiplexer_2 (
    .in0(ALU_op2), .in1(not_2_out), .out(multiplexer_2_out), .sel(Subop));  // open: en
  Multiplexer #(.select(2)) multiplexer_3 (
    .in0(comparator_1_gt), .in1(comparator_1_lt), .in2(not_3_out), .in3(comparator_1_eq), .out(branch_y_n),
    .sel(BranchOp));  // open: en
  Adder #(.width(16)) adder_1 (.a(ALU_op1), .b(ALU_op2), .out(adder_1_out));  // open: cin, cout
  Subtractor #(.width(16)) subtractor_1 (.a(ALU_op1), .b(ALU_op2), .out(subtractor_1_out));  // open: bin, bout
  Adder #(.width(16)) adder_2 (.a(ALU_op1), .b(ALU_op2), .out(adder_2_out));  // open: cin, cout
  assign and_1_out = multiplexer_1_out & multiplexer_2_out;  // AND_Gate and_1, 16 bits wide
  Multiplexer #(.width(16)) multiplexer_4 (
    .in0(adder_1_out), .in1(subtractor_1_out), .out(multiplexer_4_out), .sel(Subop));  // open: en
  Multiplexer #(.select(2), .width(16)) multiplexer_5 (
    .in0(multiplexer_4_out), .in1(adder_2_out), .in2(and_1_out), .out(ALU_output), .sel(Opcode));  // open: in3, en

  // Notes on the sheet:
  //   branch_y_n: pull=down
endmodule

module mul_div (
  input  [15:0] rs_in,
  input  [15:0] rt_in,
  input  subop,
  input  choice,
  output [15:0] LO,
  output [15:0] HI
);

  wire [15:0] divider_1_out, divider_1_rem, multiplier_1_cout, multiplier_1_out;

  Divider #(.width(16)) divider_1 (.a(rs_in), .b(rt_in), .out(divider_1_out), .rem(divider_1_rem));  // open: upper
  Multiplier #(.width(16)) multiplier_1 (
    .a(rs_in), .b(rt_in), .out(multiplier_1_out), .cout(multiplier_1_cout));  // open: cin
  Multiplexer #(.width(16)) multiplexer_1 (
    .in0(divider_1_out), .in1(multiplier_1_out), .out(LO), .sel(subop), .en(choice));
  Multiplexer #(.width(16)) multiplexer_2 (
    .in0(divider_1_rem), .in1(multiplier_1_cout), .out(HI), .sel(subop), .en(choice));
endmodule

module mlo_mhi (
  input  [15:0] LO,
  input  [15:0] HI,
  input  subop,
  input  enable,
  output [15:0] to__rs
);

  Multiplexer #(.width(16)) multiplexer_1 (.in0(LO), .in1(HI), .out(to__rs), .sel(subop), .en(enable));
endmodule

module Decoder (
  input  opcode_3,
  input  opcode_2,
  input  opcode_1,
  input  opcode_0,
  input  subop,
  output [1:0] ALU_Op,
  output BranchYes,
  output [1:0] BranchOp,
  output [1:0] JumpOp,
  output mul_div_choice,
  output [1:0] WriteSource,
  output halt,
  output put,
  output enablewrite,
  output enableread,
  output loadALUvMEM,
  output [1:0] WriteData,
  output [1:0] ALUsrc,
  output enable_mlo_mhi
);

  decoder_1 decoder_1 (
    .Opcodebit3(opcode_3), .Opcodebit2(opcode_2), .Opcodebit1(opcode_1), .Opcodebit0(opcode_0),
    .Subop(subop), .ALUop0(ALU_Op[1]), .ALUop1(ALU_Op[0]), .Branchyes(BranchYes), .BranchOp0(BranchOp[1]),
    .BranchOp1(BranchOp[0]), .Jumpop0(JumpOp[1]), .Jumpop1(JumpOp[0]), .muldivchoice(mul_div_choice));
  decoder_2 decoder_2 (
    .Opcodebit3(opcode_3), .Opcodebit2(opcode_2), .Opcodebit1(opcode_1), .Opcodebit0(opcode_0),
    .Subop(subop), .WriteSource0(WriteSource[1]), .WriteSource1(WriteSource[0]), .halt(halt), .put(put),
    .enablewrite(enablewrite), .enableread(enableread), .loadALUvMEM(loadALUvMEM), .WriteData0(WriteData[1]),
    .WriteData1(WriteData[0]));
  ALU_src alu_src_1 (
    .Opcodebit3(opcode_3), .Opcodebit2(opcode_2), .Opcodebit1(opcode_1), .Opcodebit0(opcode_0),
    .Subop(subop), .ALUsrc0(ALUsrc[1]), .ALUsrc1(ALUsrc[0]));
  mlo_mhi_decoder mlo_mhi_decoder_1 (
    .Opcodebit3(opcode_3), .Opcodebit2(opcode_2), .Opcodebit1(opcode_1), .Opcodebit0(opcode_0),
    .Subop(subop), .enable(enable_mlo_mhi));
endmodule

module decoder_1 (
  input  Opcodebit3,
  input  Opcodebit2,
  input  Opcodebit1,
  input  Opcodebit0,
  input  Subop,
  output ALUop0,
  output ALUop1,
  output Branchyes,
  output BranchOp0,
  output BranchOp1,
  output Jumpop0,
  output Jumpop1,
  output muldivchoice
);

  wire and_1_out, and_2_out, and_3_out, and_4_out, and_5_out, and_6_out, and_7_out, and_9_out, and_10_out,
       not_1_out, not_2_out, not_3_out, not_4_out, not_5_out, not_6_out, not_7_out, not_8_out, not_9_out,
       not_10_out, not_12_out, not_13_out, not_14_out, not_15_out, not_16_out;

  not not_1 (not_1_out, Opcodebit0);
  not not_2 (not_2_out, Subop);
  not not_3 (not_3_out, Opcodebit1);
  not not_4 (not_4_out, Opcodebit1);
  not not_5 (not_5_out, Opcodebit3);
  not not_6 (not_6_out, Opcodebit2);
  not not_7 (not_7_out, Opcodebit1);
  not not_8 (not_8_out, Opcodebit0);
  not not_9 (not_9_out, Opcodebit2);
  not not_10 (not_10_out, Opcodebit0);
  not not_11 (BranchOp1, Opcodebit0);
  not not_12 (not_12_out, Opcodebit0);
  not not_13 (not_13_out, Opcodebit2);
  not not_14 (not_14_out, Opcodebit1);
  not not_15 (not_15_out, Opcodebit3);
  not not_16 (not_16_out, Opcodebit2);
  and and_1 (and_1_out, Opcodebit3, not_1_out, not_2_out);
  and and_2 (and_2_out, Opcodebit3, not_3_out);
  and and_3 (and_3_out, Opcodebit2, not_4_out, Opcodebit0);
  and and_4 (and_4_out, not_5_out, Opcodebit2, Opcodebit1);
  and and_5 (and_5_out, Opcodebit3, not_6_out, not_7_out, not_8_out);
  and and_6 (and_6_out, not_9_out, not_10_out);
  and and_7 (and_7_out, Opcodebit1, Opcodebit0);
  and and_8 (Jumpop0, Opcodebit3, Opcodebit2, Opcodebit1, not_12_out);
  and and_9 (and_9_out, Opcodebit3, not_13_out, Opcodebit0);
  and and_10 (and_10_out, Opcodebit3, not_14_out, Opcodebit0);
  and and_11 (muldivchoice, not_15_out, not_16_out, Opcodebit1, Opcodebit0);
  or or_1 (ALUop0, Opcodebit1, and_1_out);
  or or_2 (ALUop1, Opcodebit0, and_2_out);
  or or_3 (Branchyes, and_3_out, and_4_out, and_5_out);
  or or_4 (BranchOp0, and_6_out, and_7_out);
  or or_5 (Jumpop1, and_9_out, and_10_out);
endmodule

module decoder_2 (
  input  Opcodebit3,
  input  Opcodebit2,
  input  Opcodebit1,
  input  Opcodebit0,
  input  Subop,
  output WriteSource0,
  output WriteSource1,
  output halt,
  output put,
  output enablewrite,
  output enableread,
  output loadALUvMEM,
  output WriteData0,
  output WriteData1
);

  wire and_5_out, and_6_out, and_7_out, and_8_out, and_9_out, and_10_out, and_11_out, and_12_out, and_13_out,
       and_14_out, and_15_out, and_16_out, and_17_out, not_1_out, not_2_out, not_3_out, not_4_out, not_5_out,
       not_6_out, not_7_out, not_8_out, not_9_out, not_10_out, not_11_out, not_12_out, not_13_out,
       not_14_out, not_15_out, not_16_out, not_17_out, not_18_out, not_19_out, not_20_out, not_21_out,
       not_22_out, not_23_out, not_24_out, not_25_out, not_26_out, not_27_out, not_28_out, not_29_out,
       not_30_out, not_31_out, not_32_out;

  not not_1 (not_1_out, Opcodebit3);
  not not_2 (not_2_out, Opcodebit1);
  not not_3 (not_3_out, Opcodebit0);
  not not_4 (not_4_out, Subop);
  not not_5 (not_5_out, Opcodebit3);
  not not_6 (not_6_out, Opcodebit1);
  not not_7 (not_7_out, Opcodebit0);
  not not_8 (not_8_out, Opcodebit2);
  not not_9 (not_9_out, Opcodebit2);
  not not_10 (not_10_out, Opcodebit0);
  not not_11 (not_11_out, Opcodebit3);
  not not_12 (not_12_out, Opcodebit2);
  not not_13 (not_13_out, Opcodebit0);
  not not_14 (not_14_out, Opcodebit3);
  not not_15 (not_15_out, Opcodebit1);
  not not_16 (not_16_out, Opcodebit2);
  not not_17 (not_17_out, Opcodebit1);
  not not_18 (not_18_out, Opcodebit1);
  not not_19 (not_19_out, Opcodebit0);
  not not_20 (not_20_out, Opcodebit2);
  not not_21 (not_21_out, Opcodebit0);
  not not_22 (not_22_out, Opcodebit3);
  not not_23 (not_23_out, Opcodebit0);
  not not_24 (not_24_out, Opcodebit0);
  not not_25 (not_25_out, Opcodebit3);
  not not_26 (not_26_out, Opcodebit1);
  not not_27 (not_27_out, Opcodebit0);
  not not_28 (not_28_out, Opcodebit2);
  not not_29 (not_29_out, Opcodebit1);
  not not_30 (not_30_out, Opcodebit3);
  not not_31 (not_31_out, Opcodebit1);
  not not_32 (not_32_out, Opcodebit0);
  and and_1 (WriteSource0, not_1_out, Opcodebit2, not_2_out, not_3_out, not_4_out);
  and and_2 (WriteSource1, not_5_out, Opcodebit2, not_6_out, not_7_out, Subop);
  and and_3 (halt, Opcodebit3, not_8_out, Opcodebit1, Opcodebit0);
  and and_4 (put, Opcodebit3, not_9_out, Opcodebit1, not_10_out);
  and and_5 (and_5_out, not_11_out, not_12_out, not_13_out);
  and and_6 (and_6_out, not_14_out, not_15_out);
  and and_7 (and_7_out, not_16_out, not_17_out, Opcodebit0);
  and and_8 (and_8_out, Opcodebit2, not_18_out, not_19_out);
  and and_9 (and_9_out, Opcodebit3, Opcodebit2, Opcodebit1, Opcodebit0);
  and and_10 (and_10_out, not_20_out, not_21_out);
  and and_11 (and_11_out, not_22_out, Opcodebit0);
  and and_12 (and_12_out, Opcodebit1, not_23_out);
  and and_13 (and_13_out, Opcodebit3, not_24_out);
  and and_14 (and_14_out, not_25_out, Opcodebit2, not_26_out, not_27_out);
  and and_15 (and_15_out, Opcodebit3, not_28_out, not_29_out, Opcodebit0);
  and and_16 (and_16_out, not_30_out, Opcodebit2, not_31_out, not_32_out);
  and and_17 (and_17_out, Opcodebit3, Opcodebit1);
  or or_1 (enablewrite, and_5_out, and_6_out, and_7_out, and_8_out, and_9_out);
  or or_2 (enableread, and_10_out, and_11_out, and_12_out, and_13_out);
  or or_3 (WriteData0, and_14_out, and_15_out);
  or or_4 (WriteData1, and_16_out, and_17_out);

  assign loadALUvMEM = Opcodebit3;
endmodule

module lw_sw_decoder (
  input  Opcodebit3,
  input  Opcodebit2,
  input  Opcodebit1,
  input  Opcodebit0,
  input  Subop,
  output lw,
  output sw
);

  wire not_1_out, not_2_out, not_3_out, not_4_out, not_5_out;

  not not_1 (not_1_out, Opcodebit1);
  not not_2 (not_2_out, Opcodebit0);
  not not_3 (not_3_out, Subop);
  not not_4 (not_4_out, Opcodebit1);
  not not_5 (not_5_out, Opcodebit0);
  and and_1 (lw, Opcodebit3, Opcodebit2, not_1_out, not_2_out, not_3_out);
  and and_2 (sw, Opcodebit3, Opcodebit2, not_4_out, not_5_out, Subop);
endmodule

module ALU_src (
  input  Opcodebit3,
  input  Opcodebit2,
  input  Opcodebit1,
  input  Opcodebit0,
  input  Subop,
  output ALUsrc0,
  output ALUsrc1
);

  wire not_1_out;

  not not_1 (not_1_out, Subop);
  and and_1 (ALUsrc1, Opcodebit0, Subop);
  and and_2 (ALUsrc0, Opcodebit0, not_1_out);
endmodule

module MAIN_PROCESSOR (
);

  wire ALU_branch_y_n, and_1_out, clock_1_out, Decoder_branchyes, Decoder_enablewrite, Decoder_halt,
       Decoder_loadaluvmem, Decoder_mul_div_choice, Decoder_put, lw_sw_decoder_lw, lw_sw_decoder_sw,
       not_1_out;
  wire [1:0] Decoder_alu_op, Decoder_alusrc, Decoder_branchop, Decoder_jumpop, Decoder_writedata,
       Decoder_writesource;
  wire [3:0] register_1_q, register_1_q_2, register_1_q_3;
  wire [7:0] adder_1_out, bit_extender_4_out, multiplexer_3_out, multiplexer_4_out, PC_q;
  wire [15:0] ALU_alu_output, bit_extender_1_out, bit_extender_2_out, bit_extender_3_out, HI_q, LO_q,
       mul_div_hi, mul_div_lo, multiplexer_1_out, multiplexer_2_out, multiplexer_5_out, ram_1_data,
       Register_File_read_data1, Register_File_read_data2, rom_1_data;
  wire [15:12] register_1_q_4;

  Register PC (.D(multiplexer_4_out), .en(not_1_out), .Q(PC_q), .clk(clock_1_out));  // open: clr
  Clock clock_1 (.out(clock_1_out));
  not not_1 (not_1_out, Decoder_halt);
  Adder adder_1 (.a(8'h1), .b(PC_q), .out(adder_1_out));  // open: cin, cout
  ROM #(.dataWidth(16)) rom_1 (.addr(PC_q), .data(rom_1_data));  // open: sel
  assign bit_extender_1_out = {{8{1'b0}}, adder_1_out};  // Bit_Extender bit_extender_1
  Decoder Decoder (
    .opcode_3(rom_1_data[15]), .opcode_2(rom_1_data[14]), .opcode_1(rom_1_data[13]),
    .opcode_0(rom_1_data[12]), .subop(rom_1_data[0]), .ALU_Op(Decoder_alu_op), .BranchYes(Decoder_branchyes),
    .BranchOp(Decoder_branchop), .JumpOp(Decoder_jumpop), .mul_div_choice(Decoder_mul_div_choice),
    .WriteSource(Decoder_writesource), .halt(Decoder_halt), .put(Decoder_put),
    .enablewrite(Decoder_enablewrite), .loadALUvMEM(Decoder_loadaluvmem), .WriteData(Decoder_writedata),
    .ALUsrc(Decoder_alusrc));  // open: enableread, enable_mlo_mhi
  lw_sw_decoder lw_sw_decoder (
    .Opcodebit3(rom_1_data[15]), .Opcodebit2(rom_1_data[14]), .Opcodebit1(rom_1_data[13]),
    .Opcodebit0(rom_1_data[12]), .Subop(rom_1_data[0]), .lw(lw_sw_decoder_lw), .sw(lw_sw_decoder_sw));
  Multiplexer #(.select(2), .width(16)) multiplexer_1 (
    .in0(multiplexer_5_out), .in1(bit_extender_2_out), .in2(bit_extender_1_out), .out(multiplexer_1_out),
    .sel(Decoder_writedata));  // open: in3, en
  assign bit_extender_2_out = {{8{1'b0}}, rom_1_data[8:1]};  // Bit_Extender bit_extender_2
  assign bit_extender_3_out = {{8{rom_1_data[8]}}, rom_1_data[8:1]};  // Bit_Extender bit_extender_3
  Register_File Register_File (
    .WriteSource(Decoder_writesource), .Write_Data(multiplexer_1_out), .HI(HI_q), .LO(LO_q),
    .WriteRegister(rom_1_data[11:9]), .enable_write(Decoder_enablewrite),
    .Write_Register_Enabler(rom_1_data[11:9]), .read_reg1(rom_1_data[11:9]), .Clock(clock_1_out),
    .read_reg2(rom_1_data[8:6]), .read_data1(Register_File_read_data1), .read_data2(Register_File_read_data2));
  // Probe on Register_File_read_data1
  mul_div mul_div (
    .rs_in(Register_File_read_data1), .rt_in(Register_File_read_data2), .subop(rom_1_data[0]),
    .LO(mul_div_lo), .HI(mul_div_hi), .choice(Decoder_mul_div_choice));
  Bit_Extender #(.in_width(16), .out_width(8)) bit_extender_4 (.in(Register_File_read_data1), .out(bit_extender_4_out));
  Multiplexer #(.select(2), .width(16)) multiplexer_2 (
    .in0(Register_File_read_data2), .in1(bit_extender_2_out), .in2(bit_extender_3_out),
    .out(multiplexer_2_out), .sel(Decoder_alusrc));  // open: in3, en
  Register #(.width(16)) LO (.D(mul_div_lo), .Q(LO_q), .clk(clock_1_out));  // open: en, clr
  Register #(.width(16)) HI (.D(mul_div_hi), .Q(HI_q), .clk(clock_1_out));  // open: en, clr
  Multiplexer #(.width(8)) multiplexer_3 (
    .in0(adder_1_out), .in1(rom_1_data[8:1]), .out(multiplexer_3_out), .sel(and_1_out));  // open: en
  and and_1 (and_1_out, ALU_branch_y_n, Decoder_branchyes);
  LED led_1 (.in(Decoder_halt));
  Multiplexer #(.select(2), .width(8)) multiplexer_4 (
    .in0(multiplexer_3_out), .in1(rom_1_data[8:1]), .in2(bit_extender_4_out), .out(multiplexer_4_out),
    .sel(Decoder_jumpop));  // open: in3, en
  ALU ALU (
    .ALU_op1(Register_File_read_data1), .ALU_op2(multiplexer_2_out), .branch_y_n(ALU_branch_y_n),
    .BranchOp(Decoder_branchop), .Subop(rom_1_data[0]), .Opcode(Decoder_alu_op), .ALU_output(ALU_alu_output));
  Hex_Digit_Display hex_digit_display_1 (.value(register_1_q_4));  // open: dp
  Hex_Digit_Display hex_digit_display_2 (.value(register_1_q_3));  // open: dp
  Register #(.width(16)) register_1 (
    .D(Register_File_read_data1), .en(Decoder_put),
    .Q({register_1_q_4, register_1_q_3, register_1_q_2, register_1_q}), .clk(clock_1_out));  // open: clr
  RAM #(.dataWidth(16), .bus("separate")) ram_1 (
    .addr(Register_File_read_data2[7:0]), .din(Register_File_read_data1), .data(ram_1_data),
    .str(lw_sw_decoder_sw), .clk(clock_1_out), .ld(lw_sw_decoder_lw));  // open: sel, clr
  Hex_Digit_Display hex_digit_display_3 (.value(register_1_q));  // open: dp
  Hex_Digit_Display hex_digit_display_4 (.value(register_1_q_2));  // open: dp
  Multiplexer #(.width(16)) multiplexer_5 (
    .in0(ALU_alu_output), .in1(ram_1_data), .out(multiplexer_5_out), .sel(Decoder_loadaluvmem));  // open: en

  // Notes on the sheet:
  //   Erik Dash
  //   erd53@pitt.edu
  //   PC + 1
  //   Instructions (ROM)
  //   write data selector
  //   $rs value probe
  //   Branches
  //   ALU second input selector
  //   Jumps
  //   Data (RAM)
  //   write from memory vs from ALU output
endmodule

module mlo_mhi_decoder (
  input  Opcodebit3,
  input  Opcodebit2,
  input  Opcodebit1,
  input  Opcodebit0,
  input  Subop,
  output enable
);

  wire not_1_out, not_2_out, not_3_out;

  not not_1 (not_1_out, Opcodebit3);
  not not_2 (not_2_out, Opcodebit1);
  not not_3 (not_3_out, Opcodebit0);
  and and_1 (enable, not_1_out, Opcodebit2, not_2_out, not_3_out);
endmodule
